// Logisim project 2 BIT MULTIPLICATION.circ as structural Verilog: 5 circuits, main circuit binary2bcd
module binary2bcd (
  input  b7,
  input  b6,
  input  b5,
  input  b4,
  input  b3,
  input  b2,
  input  b1,
  input  b0,
  output q0,
  output q1,
  output q2,
  output q3,
  output q4,
  output q5,
  output q6,
  output q7,
  output q8,
  output q9
);

  wire add_3_1_s0, add_3_1_s1, add_3_1_s2, add_3_1_s3, add_3_2_s0, add_3_2_s1, add_3_2_s2, add_3_2_s3,
       add_3_3_s0, add_3_3_s1, add_3_3_s2, add_3_3_s3, add_3_4_s0, add_3_4_s1, add_3_4_s2, add_3_6_s0,
       add_3_6_s1, add_3_6_s2, add_3_6_s3;

  ADD_3 add_3_1 (
    .i2(b7), .i3(1'b0), .i0(b5), .i1(b6), .s1(add_3_1_s1), .S2(add_3_1_s2), .S3(add_3_1_s3), .s0(add_3_1_s0));
  ADD_3 add_3_2 (
    .i2(add_3_1_s1), .i3(add_3_1_s2), .i0(b4), .i1(add_3_1_s0), .s1(add_3_2_s1), .S2(add_3_2_s2),
    .S3(add_3_2_s3), .s0(add_3_2_s0));
  ADD_3 add_3_3 (
    .i2(add_3_2_s1), .i3(add_3_2_s2), .i0(b3), .i1(add_3_2_s0), .s1(add_3_3_s1), .S2(add_3_3_s2),
    .S3(add_3_3_s3), .s0(add_3_3_s0));
  ADD_3 add_3_4 (
    .i2(add_3_1_s3), .i3(1'b0), .i0(add_3_3_s3), .i1(add_3_2_s3), .s1(add_3_4_s1), .S2(add_3_4_s2), .S3(q9),
    .s0(add_3_4_s0));
  ADD_3 add_3_5 (
    .i2(add_3_4_s1), .i3(add_3_4_s2), .i0(add_3_6_s3), .i1(add_3_4_s0), .s1(q6), .S2(q7), .S3(q8), .s0(q5));
  ADD_3 add_3_6 (
    .i2(add_3_3_s1), .i3(add_3_3_s2), .i0(b2), .i1(add_3_3_s0), .s1(add_3_6_s1), .S2(add_3_6_s2),
    .S3(add_3_6_s3), .s0(add_3_6_s0));
  ADD_3 add_3_7 (.i2(add_3_6_s1), .i3(add_3_6_s2), .i0(b1), .i1(add_3_6_s0), .s1(q2), .S2(q3), .S3(q4), .s0(q1));

  assign q0 = b0;
endmodule

module ADD_3 (
  input  i2,
  input  i3,
  input  i0,
  input  i1,
  output S2,
  output S3,
  output s1,
  output s0
);

  wire and_2_p8, i0_t, i0i2, i1_t, i1i0, i2_ni1, i2_t, i2i1, i2i1_ni0, i2i1_t, i2i1i0, i3_ni2_ni0, i3_t,
       i3i0, i3i0_t, or_2_p8, or_p3, or_p14;

  // _7432 or: pin names not known; wires that end beside it: i3, i0i2, or_p3, or_p3, i2i1, S3, 1'b0, 1'b1, i3i0, i2i1_ni0, S2, i2_ni1, i1i0, or_p14
  // _7432 or_2: pin names not known; wires that end beside it: or_p14, i3i0_t, s1, 1'b0, 1'b1, i3i0_t, i2i1i0, or_2_p8, or_2_p8, i3_ni2_ni0, s0
  // _7408 and: pin names not known; wires that end beside it: i2, i0, i0i2, i2, i1, i2i1, 1'b0, 1'b1, i3, i0, i3i0, i2, i1_t, i2i1_t
  // _7408 and_2: pin names not known; wires that end beside it: i2i1, i0_t, i2i1i0, 1'b0, 1'b1, i3_t, i2_t, and_2_p8, and_2_p8, i0, i3_ni2_ni0
  // _7404 not: pin names not known; wires that end beside it: i1, i1_t, i2, i2_t, i3, i3_t, 1'b0, 1'b1, i0, i0_t
  // _7408 and_3: pin names not known; wires that end beside it: i2i1_t, i0_t, i2i1_ni0, i2_t, i1, i2_ni1, 1'b0, 1'b1, i1, i0, i1i0, i3, i0_t, i3i0_t
endmodule

module _1BitAdder (
  input  cin,
  input  a,
  input  a_2,
  output cout,
  output s
);

  // _7483 7483_1: pin names not known; wires that end beside it: 1'b0, 1'b0, 1'b0, 1'b1, cout, 1'b0, 1'b0, 1'b0, 1'b0, cin, 1'b0, a, a_2, s, s
endmodule

module mult (
  input  B1,
  input  A0,
  input  As,
  input  B0,
  input  Bs,
  input  A1,
  input  A2,
  input  B2,
  output Z0,
  output Zs,
  output Z1,
  output Z2,
  output Z3,
  output Z4,
  output Z5
);

  wire A0B2, A1B1, A1B2, A2B0, A2B1, A2B2, binary2bcd_1_q0, binary2bcd_1_q1, binary2bcd_1_q2,
       binary2bcd_1_q3, binary2bcd_1_q4, binary2bcd_1_q5, binary2bcd_1_q6, binary2bcd_1_q7, binary2bcd_1_q8,
       binary2bcd_1_q9, n1bitadder_1_cout, n1bitadder_2_cout, n1bitadder_2_s, n1bitadder_3_cout,
       n1bitadder_3_s, n1bitadder_4_cout, n1bitadder_5_cout, n7408_1_p6, n7408_1_p11, n7448_1_p11,
       n7448_1_p12, n7448_1_p13, n7448_1_p14, n7448_1_p15, n7448_1_p16, n7448_1_p17, n7448_2_p5, n7448_2_p6,
       n7448_2_p7, n7448_2_p8, n7448_2_p9, n7448_2_p10, n7448_2_p11;

  // _7408 7408_1: pin names not known; wires that end beside it: A0, B0, Z0, B0, A1, n7408_1_p6, 1'b0, 1'b1, A0, B1, n7408_1_p11, A1, B1, A1B1
  // _7408 7408_2: pin names not known; wires that end beside it: A2, B2, A2B2, B2, A1, 1'b1
  // _7408 7408_3: pin names not known; wires that end beside it: B2, A0, A0B2, B0, A2, A2B0, 1'b0, A1B2, 1'b0, 1'b1, A2, B1, A2B1
  _1BitAdder u_1bitadder_1 (.cin(1'b0), .a_2(n7408_1_p11), .a(n7408_1_p6), .cout(n1bitadder_1_cout), .s(Z1));
  _1BitAdder u_1bitadder_2 (
    .cin(n1bitadder_1_cout), .a_2(A1B1), .a(A2B0), .cout(n1bitadder_2_cout), .s(n1bitadder_2_s));
  _1BitAdder u_1bitadder_3 (
    .cin(n1bitadder_2_cout), .a_2(1'b0), .a(A2B1), .cout(n1bitadder_3_cout), .s(n1bitadder_3_s));
  _1BitAdder u_1bitadder_4 (.cin(n1bitadder_2_s), .a_2(A0B2), .a(1'b0), .cout(n1bitadder_4_cout), .s(Z2));
  _1BitAdder u_1bitadder_5 (.cin(n1bitadder_4_cout), .a_2(n1bitadder_3_s), .a(A1B2), .cout(n1bitadder_5_cout), .s(Z3));
  _1BitAdder u_1bitadder_6 (.cin(n1bitadder_5_cout), .a_2(n1bitadder_3_cout), .a(A2B2), .cout(Z5), .s(Z4));
  // _7486 7486_1: pin names not known; wires that end beside it: As, Bs, Zs, 1'b0, 1'b1
  binary2bcd binary2bcd_1 (
    .b7(1'b0), .b6(1'b0), .b5(Z5), .b4(Z4), .b3(Z3), .b2(Z2), .b1(Z1), .b0(Z0), .q9(binary2bcd_1_q9),
    .q8(binary2bcd_1_q8), .q7(binary2bcd_1_q7), .q6(binary2bcd_1_q6), .q5(binary2bcd_1_q5),
    .q4(binary2bcd_1_q4), .q3(binary2bcd_1_q3), .q2(binary2bcd_1_q2), .q1(binary2bcd_1_q1),
    .q0(binary2bcd_1_q0));
  // _7_Segment_Display 7_segment_display_1: pin names not known; wires that end beside it: Zs, binary2bcd_1_q7, binary2bcd_1_q4, 1'b0
  // _7448 7448_1: pin names not known; wires that end beside it: binary2bcd_1_q9, binary2bcd_1_q8, binary2bcd_1_q1, binary2bcd_1_q2, 1'b1, 1'b1, binary2bcd_1_q3, binary2bcd_1_q0, 1'b0, 1'b1, n7448_1_p11, n7448_1_p12, n7448_1_p13, n7448_1_p14, n7448_1_p15, n7448_1_p16, n7448_1_p17
  // _7448 7448_2: pin names not known; wires that end beside it: binary2bcd_1_q5, binary2bcd_1_q6, 1'b1, 1'b1, n7448_2_p5, n7448_2_p6, n7448_2_p7, n7448_2_p8, n7448_2_p9, n7448_2_p10, n7448_2_p11
  _7_Segment_Display u_7_segment_display_2 (
    .g(n7448_2_p6), .f(n7448_2_p5), .a(n7448_2_p7), .b(n7448_2_p8), .e(n7448_2_p11), .d(n7448_2_p10),
    .c(n7448_2_p9));  // open: dp
  _7_Segment_Display u_7_segment_display_3 (
    .g(n7448_1_p12), .f(n7448_1_p11), .a(n7448_1_p13), .b(n7448_1_p14), .e(n7448_1_p17), .d(n7448_1_p16),
    .c(n7448_1_p15));  // open: dp
endmodule

module mult2 (
  input  A0,
  input  AS,
  input  A1,
  input  BS,
  input  B0,
  input  B1,
  output MS,
  output M0,
  output M1,
  output M2,
  output M3
);

  wire n7408_1_p3, n7408_1_p6, n7408_1_p10, n7408_1_p13;

  // _7408 7408_1: pin names not known; wires that end beside it: A0, B0, n7408_1_p3, B0, A1, n7408_1_p6, 1'b0, A0, B1, n7408_1_p10, B1, A1, n7408_1_p13
  // _7483 7483_1: pin names not known; wires that end beside it: 1'b0, M2, 1'b0, n7408_1_p13, 1'b1, M1, n7408_1_p10, n7408_1_p6, 1'b0, M3, 1'b0, 1'b0, 1'b0, 1'b0, n7408_1_p3, M0
  // _7486 7486_1: pin names not known; wires that end beside it: AS, BS, MS
endmodule
