// Logisim project 2 BIT REM.circ as structural Verilog
module _2x1 (
  input  i0,
  input  i1,
  input  s0,
  output out_4
);

  wire n7404_1_p2, n7408_1_p3, n7408_1_p6;

  // _7404 7404_1: pin names not known; wires that end beside it: s0, n7404_1_p2
  // _7408 7408_1: pin names not known; wires that end beside it: i0, n7404_1_p2, n7408_1_p3, s0, i1, n7408_1_p6
  // _7432 7432_1: pin names not known; wires that end beside it: n7408_1_p6, n7408_1_p3, out_4
endmodule

// Remainder
module Final_step (
  input  A1,
  input  A0,
  input  B1,
  input  B0,
  output Div0,
  output C1,
  output C0
);

  wire C0_t, C1_t, OR_p3, OR_p6;

  _2_bit_rem u_2_bit_rem_1 (.A1(A1), .A0(A0), .B1(B1), .B0(B0), .C1(C1_t), .C0(C0_t));
  // _7432 OR: pin names not known; wires that end beside it: B0, B1, OR_p3, OR_p3, 1'b0, OR_p6, 1'b0, 1'b1
  // _7404 7404_1: pin names not known; wires that end beside it: OR_p6, Div0, 1'b0, 1'b1
  // _7408 7408_1: pin names not known; wires that end beside it: 1'b0, 1'b1, C0_t, OR_p6, C0, OR_p6, C1_t, C1
endmodule

// X-B
module Subtractor (
  input  Bin,
  input  A,
  input  B,
  output Ans,
  output Bout
);

  wire AND_p3, AND_p6, NOT_p2, NOT_p4, XOR_p3;

  // _7486 XOR: pin names not known; wires that end beside it: A, B, XOR_p3, XOR_p3, Bin, Ans, 1'b0, 1'b1
  // _7404 NOT: pin names not known; wires that end beside it: A, NOT_p2, XOR_p3, NOT_p4, 1'b0, 1'b1
  // _7408 AND: pin names not known; wires that end beside it: NOT_p2, B, AND_p3, NOT_p4, Bin, AND_p6, 1'b0, 1'b1
  // _7432 OR: pin names not known; wires that end beside it: AND_p3, AND_p6, Bout, 1'b0, 1'b1
endmodule

module _2_bit_rem (
  input  A1,
  input  A0,
  input  B1,
  input  B0,
  output C1,
  output C0
);

  wire n2x1_1_out_4, subtractor_1_ans, subtractor_1_bout, subtractor_2_ans, subtractor_2_bout,
       subtractor_3_ans, subtractor_3_bout, subtractor_4_ans, subtractor_4_bout;

  Subtractor subtractor_1 (.A(A1), .B(B0), .Bin(1'b0), .Bout(subtractor_1_bout), .Ans(subtractor_1_ans));
  Subtractor subtractor_2 (.A(1'b0), .B(B1), .Bin(subtractor_1_bout), .Bout(subtractor_2_bout), .Ans(subtractor_2_ans));
  _2x1 u_2x1_1 (.i0(subtractor_1_ans), .i1(A1), .s0(subtractor_2_bout), .out_4(n2x1_1_out_4));
  Subtractor subtractor_3 (.A(n2x1_1_out_4), .B(B1), .Bin(1'b0), .Bout(subtractor_3_bout), .Ans(subtractor_3_ans));
  Subtractor subtractor_4 (.A(A0), .B(B0), .Bin(subtractor_3_bout), .Bout(subtractor_4_bout), .Ans(subtractor_4_ans));
  _2x1 u_2x1_2 (.i0(subtractor_3_ans), .i1(n2x1_1_out_4), .s0(subtractor_4_bout), .out_4(C1));
  _2x1 u_2x1_3 (.i0(subtractor_4_ans), .i1(A0), .s0(subtractor_4_bout), .out_4(C0));
endmodule
