// Logisim project 2 BITS.circ as structural Verilog: 2 circuits, main circuit ADDER B HOWRTO
module ADDER_B_HOWRTO (
  input  B2,
  input  B1,
  input  B0,
  input  A2,
  input  A1,
  input  A0,
  input  A0_S1,
  output out_8,
  output O3,
  output O2,
  output O1
);

  wire A_B, A_B_t, ADD_SIGN, B_A, BS_t, C, C1, c1_t, c1_t_t, C2, C3, C3_t, C_t, O1_t, S1, S2, S3, SIGN,
       SUB_SIGN;

  add_subtract add_subtract_1 (.a0(A0), .s1(C1), .s2(C2), .carr(C3), .control(C), .a1(A1), .b0(B0), .b1(B1));
  // IC_7485 ic_7485_1: pin names not known; wires that end beside it: A0, A1, 1'b0, 1'b0, B0, B1, 1'b0, 1'b0, 1'b0, 1'b1, 1'b0, B_A, A_B, A_B_t
  // _74153 74153_1: pin names not known; wires that end beside it: 1'b0, C, 1'b0, SIGN, SIGN, SIGN, out_8, 1'b0, 1'b1, A_B, 1'b0, 1'b0, 1'b0, 1'b0
  // _7408 7408_1: pin names not known; wires that end beside it: C, C3_t, O1_t, 1'b0, 1'b1
  // _7483 7483_1: pin names not known; wires that end beside it: O3, 1'b0, S3, 1'b1, O2, S2, 1'b0, 1'b0, 1'b0, S1, O1_t, O1
  // _74157 74157_1: pin names not known; wires that end beside it: A0_S1, c1_t, c1_t_t, C, ADD_SIGN, SUB_SIGN, SIGN, 1'b0, 1'b1, 1'b0, 1'b0, 1'b0, 1'b0, 1'b0
  // _7486 7486_1: pin names not known; wires that end beside it: A2, B2, c1_t, 1'b0, 1'b1, C1, O1_t, S1, C2, O1_t, S2
  // _74157 74157_2: pin names not known; wires that end beside it: C, C3, 1'b0, S3, 1'b0, 1'b0, 1'b0, 1'b1, 1'b0, 1'b0, 1'b0, 1'b0, 1'b0
  // _7404 7404_1: pin names not known; wires that end beside it: C3, C3_t, C, C_t, c1_t, c1_t_t, 1'b0, 1'b1, B2, BS_t
  // _74157 74157_3: pin names not known; wires that end beside it: B_A, A2, B2, ADD_SIGN, A2, BS_t, SUB_SIGN, 1'b0, 1'b1, 1'b0, 1'b0, 1'b0, 1'b0, 1'b0

  // Other names for the same wires on the sheet: AS = A2; BS = B2; F1 = O1; F2 = O2; F3 = O3; SS = out_8
endmodule

module CIRCUIT_ADD_SUB (
  input  a0,
  input  a1,
  input  b0,
  input  control,
  input  b1,
  output s1,
  output carr,
  output s2
);

  wire co, o0, o1;

  // _7486 7486_1: pin names not known; wires that end beside it: control, b0, o0, control, b1, o1, 1'b0, 1'b1
  // _7483 7483_1: pin names not known; wires that end beside it: 1'b0, 1'b0, 1'b0, 1'b1, co, 1'b0, 1'b0, 1'b0, control, 1'b0, a0, o0, s1
  // _7483 7483_2: pin names not known; wires that end beside it: 1'b0, 1'b0, 1'b0, 1'b1, carr, 1'b0, 1'b0, 1'b0, co, 1'b0, a1, o1, s2
endmodule
