// Logisim project AdderSubtractorProject.circ as structural Verilog: 3 circuits, main circuit CONTROLS
// C
module CONTROLS (
  input  as,
  input  ADD_0__SUB1,
  input  bs,
  output control
);

  wire c1, c1_t;

  // _7486 7486_1: pin names not known; wires that end beside it: as, bs, c1, 1'b0, 1'b1
  // _7404 7404_1: pin names not known; wires that end beside it: c1, c1_t, 1'b0, 1'b1
  // _74157 74157_1: pin names not known; wires that end beside it: ADD_0__SUB1, c1, c1_t, control, 1'b0, 1'b0, 1'b0, 1'b1, 1'b0, 1'b0, 1'b0, 1'b0, 1'b0
endmodule

module add_subtract (
  input  a0,
  input  a1,
  input  b0,
  input  control,
  input  b1,
  output s1,
  output carr,
  output s2
);

  wire co, o0, o1;

  // _7486 7486_1: pin names not known; wires that end beside it: control, b0, o0, control, b1, o1, 1'b0, 1'b1
  // _7483 7483_1: pin names not known; wires that end beside it: 1'b0, 1'b0, 1'b0, 1'b1, co, 1'b0, 1'b0, 1'b0, control, 1'b0, a0, o0, s1
  // _7483 7483_2: pin names not known; wires that end beside it: 1'b0, 1'b0, 1'b0, 1'b1, carr, 1'b0, 1'b0, 1'b0, co, 1'b0, a1, o1, s2
endmodule

module \final  (
  input  B2,
  input  B1,
  input  B0,
  input  A2,
  input  A1,
  input  A0,
  input  A0_S1,
  output O3,
  output O2,
  output O1
);

  wire C, C1, C2, C3, C3_t, C_t, O1_t, S1, S2, S3;

  CONTROLS controls_1 (.as(A2), .ADD_0__SUB1(A0_S1), .bs(B2), .control(C));
  add_subtract add_subtract_1 (.a0(A0), .s1(C1), .s2(C2), .carr(C3), .control(C), .a1(A1), .b0(B0), .b1(B1));
  // _7408 7408_1: pin names not known; wires that end beside it: C, C3_t, O1_t, 1'b0, 1'b1
  // _74157 74157_1: pin names not known; wires that end beside it: C, C3, 1'b0, S3, 1'b0, 1'b0, 1'b0, 1'b1, 1'b0, 1'b0, 1'b0, 1'b0, 1'b0
  // _7483 7483_1: pin names not known; wires that end beside it: O3, 1'b0, S3, 1'b1, O2, S2, 1'b0, 1'b0, 1'b0, S1, O1_t, O1
  // _7404 7404_1: pin names not known; wires that end beside it: C3, C3_t, C, C_t, 1'b0, 1'b1
  // _7486 7486_1: pin names not known; wires that end beside it: 1'b0, 1'b1, C1, O1_t, S1, C2, O1_t, S2

  // Other names for the same wires on the sheet: AS = A2; BS = B2; F1 = O1; F2 = O2; F3 = O3
endmodule
