// Logisim project FINAL.circ as structural Verilog: 4 circuits, main circuit main
module main (
  input  AS,
  input  A2,
  input  A1,
  input  A0,
  input  BS,
  input  B2,
  input  B1,
  input  B0,
  input  C1,
  input  C0,
  output D5,
  output D4,
  output D3,
  output Div0,
  output D2,
  output D1,
  output D0,
  output DS,
  output F0
);

  wire DIVISON_BY_0, DS_t, n7404_1_p1, n7408_1_p3, n7432_1_p3, n7432_1_p6, n7432_1_p9, n7432_1_p12, R0, R1,
       R2, RS, S0, S1, S2, SS, Z0, Z1, Z2, Z3, Z4, Z5, ZS;

  // _7404 7404_1: pin names not known; wires that end beside it: n7404_1_p1, F0
  // _7432 7432_1: pin names not known; wires that end beside it: D0, D1, n7432_1_p3, n7432_1_p3, D2, n7432_1_p6, n7432_1_p6, D3, n7432_1_p9, n7432_1_p9, D4, n7432_1_p12
  Final_Rem final_rem_1 (
    .As(AS), .A2(A2), .A1(A1), .A0(A0), .Bs(BS), .B2(B2), .B1(B1), .B0(B0), .Div0(DIVISON_BY_0), .Cs(RS),
    .C2(R2), .C1(R1), .C0(R0));
  // _7408 7408_1: pin names not known; wires that end beside it: DIVISON_BY_0, C1, n7408_1_p3, n7408_1_p3, C0, Div0
  mult mult_1 (
    .B1(B1), .A0(A0), .As(AS), .B0(B0), .Bs(BS), .Zs(ZS), .A1(A1), .A2(A2), .B2(B2), .Z1(Z1), .Z2(Z2),
    .Z3(Z3), .Z4(Z4), .Z0(Z0), .Z5(Z5));
  // _7432 7432_2: pin names not known; wires that end beside it: n7432_1_p12, D4, n7404_1_p1
  _2x1 u_2x1_1 (.i0(DS_t), .i1(1'b0), .s0(F0), .out_4(DS));
  \final  final_1 (.O3(S2), .O2(S1), .O1(S0), .B2(BS), .B1(B1), .B0(B0), .A2(AS), .A1(A1), .A0(A0), .A0_S1(C0));
  // SIGNS signs_1: pin names not known; wires that end beside it: A1, A0, A2, B2, B1, B0, C0, AS, BS, SS
  _4x1 u_4x1_1 (.i0(SS), .i2(ZS), .i1(SS), .i3(RS), .s0(C0), .s1(C1), .o(DS_t));
  _4x1 u_4x1_2 (.i0(1'b0), .i2(Z5), .i1(1'b0), .i3(1'b0), .s0(C0), .s1(C1), .o(D5));
  _4x1 u_4x1_3 (.i0(1'b0), .i2(Z4), .i1(1'b0), .i3(1'b0), .s0(C0), .s1(C1), .o(D4));
  _4x1 u_4x1_4 (.i0(1'b0), .i2(Z3), .i1(1'b0), .i3(1'b0), .s0(C0), .s1(C1), .o(D3));
  _4x1 u_4x1_5 (.i0(S2), .i2(Z2), .i1(S2), .i3(R2), .s0(C0), .s1(C1), .o(D2));
  _4x1 u_4x1_6 (.i0(S1), .i2(Z1), .i1(S1), .i3(R1), .s0(C0), .s1(C1), .o(D1));
  _4x1 u_4x1_7 (.i0(S0), .i2(Z0), .i1(S0), .i3(R0), .s0(C0), .s1(C1), .o(D0));

  // Other names for the same wires on the sheet: DSF = DS
endmodule

module SIGNS (
  input  A0,
  input  A1,
  input  B0,
  input  B1,
  input  A0_S1,
  input  AS,
  input  BS,
  output out_8
);

  wire A_B, A_B_t, ADD_SIGN, B_A, BS_t, C, SIGN, SUB_SIGN;

  // _74157 74157_1: pin names not known; wires that end beside it: B_A, AS, BS, ADD_SIGN, AS, BS_t, SUB_SIGN, 1'b0, 1'b1, 1'b0, 1'b0, 1'b0, 1'b0, 1'b0
  // _74157 74157_2: pin names not known; wires that end beside it: A0_S1, ADD_SIGN, SUB_SIGN, SIGN, 1'b0, 1'b0, 1'b0, 1'b1, 1'b0, 1'b0, 1'b0, 1'b0, 1'b0
  CONTROLS controls_1 (.as(AS), .ADD_0__SUB1(A0_S1), .bs(BS), .control(C));
  // _7404 7404_1: pin names not known; wires that end beside it: BS, BS_t, 1'b0, 1'b1
  // _74153 74153_1: pin names not known; wires that end beside it: C, 1'b0, SIGN, SIGN, SIGN, out_8, 1'b0, 1'b1, A_B, 1'b0, 1'b0, 1'b0, 1'b0
  // IC_7485 ic_7485_1: pin names not known; wires that end beside it: A0, A1, 1'b0, 1'b0, B0, B1, 1'b0, 1'b0, 1'b0, 1'b1, 1'b0, B_A, A_B, A_B_t

  // Other names for the same wires on the sheet: SS = out_8
endmodule

module ALU (
  input  AS,
  input  A2,
  input  A1,
  input  A0,
  input  BS,
  input  B2,
  input  B1,
  input  B0,
  input  C1,
  input  C0
);

  wire binary2bcd_1_q0, binary2bcd_1_q1, binary2bcd_1_q2, binary2bcd_1_q3, binary2bcd_1_q4, binary2bcd_1_q5,
       binary2bcd_1_q6, binary2bcd_1_q7, binary2bcd_1_q8, binary2bcd_1_q9, main_1_d0, main_1_d1, main_1_d2,
       main_1_d3, main_1_d4, main_1_d5, main_1_div0, main_1_f0, n7448_1_p11, n7448_1_p12, n7448_1_p13,
       n7448_1_p14, n7448_1_p15, n7448_1_p16, n7448_1_p17, n7448_2_p9, n7448_2_p10, n7448_2_p11, n7448_2_p12,
       n7448_2_p13, n7448_2_p14, n7448_2_p15, SS;

  LED ZERO_FLAG (.in(main_1_f0));
  main main_1 (
    .AS(AS), .A2(A2), .A1(A1), .A0(A0), .BS(BS), .B2(B2), .B1(B1), .B0(B0), .C1(C1), .C0(C0), .D5(main_1_d5),
    .D4(main_1_d4), .D3(main_1_d3), .Div0(main_1_div0), .D2(main_1_d2), .D1(main_1_d1), .D0(main_1_d0),
    .F0(main_1_f0), .DS(SS));
  LED DIV0FLAG (.in(main_1_div0));
  binary2bcd binary2bcd_1 (
    .b7(1'b0), .b6(1'b0), .b5(main_1_d5), .b4(main_1_d4), .b3(main_1_d3), .b2(main_1_d2), .b1(main_1_d1),
    .b0(main_1_d0), .q9(binary2bcd_1_q9), .q8(binary2bcd_1_q8), .q7(binary2bcd_1_q7), .q6(binary2bcd_1_q6),
    .q5(binary2bcd_1_q5), .q4(binary2bcd_1_q4), .q3(binary2bcd_1_q3), .q2(binary2bcd_1_q2),
    .q1(binary2bcd_1_q1), .q0(binary2bcd_1_q0));
  _7_Segment_Display u_7_segment_display_1 (.g(SS));  // open: f, a, b, e, d, c, dp
  // _7448 7448_1: pin names not known; wires that end beside it: binary2bcd_1_q9, binary2bcd_1_q8, binary2bcd_1_q1, binary2bcd_1_q2, 1'b1, 1'b1, binary2bcd_1_q3, binary2bcd_1_q0, 1'b0, 1'b1, n7448_1_p11, n7448_1_p12, n7448_1_p13, n7448_1_p14, n7448_1_p15, n7448_1_p16, n7448_1_p17
  // _7448 7448_2: pin names not known; wires that end beside it: binary2bcd_1_q5, binary2bcd_1_q6, 1'b1, 1'b1, binary2bcd_1_q7, binary2bcd_1_q4, 1'b0, 1'b1, n7448_2_p9, n7448_2_p10, n7448_2_p11, n7448_2_p12, n7448_2_p13, n7448_2_p14, n7448_2_p15
  _7_Segment_Display u_7_segment_display_2 (
    .g(n7448_2_p10), .f(n7448_2_p9), .a(n7448_2_p11), .b(n7448_2_p12), .e(n7448_2_p15), .d(n7448_2_p14),
    .c(n7448_2_p13));  // open: dp
  _7_Segment_Display u_7_segment_display_3 (
    .g(n7448_1_p12), .f(n7448_1_p11), .a(n7448_1_p13), .b(n7448_1_p14), .e(n7448_1_p17), .d(n7448_1_p16),
    .c(n7448_1_p15));  // open: dp
endmodule

module FF (
);

  wire binary2bcd_1_q0, binary2bcd_1_q1, binary2bcd_1_q2, binary2bcd_1_q3, binary2bcd_1_q4, binary2bcd_1_q5,
       binary2bcd_1_q6, binary2bcd_1_q7, binary2bcd_1_q8, binary2bcd_1_q9, n7448_1_p11, n7448_1_p12,
       n7448_1_p13, n7448_1_p14, n7448_1_p15, n7448_1_p16, n7448_1_p17, n7448_2_p1, n7448_2_p9, n7448_2_p10,
       n7448_2_p11, n7448_2_p12, n7448_2_p13, n7448_2_p14, n7448_2_p15;

  binary2bcd binary2bcd_1 (
    .b7(1'b0), .b6(1'b0), .q9(binary2bcd_1_q9), .q8(binary2bcd_1_q8), .q7(binary2bcd_1_q7),
    .q6(binary2bcd_1_q6), .q5(binary2bcd_1_q5), .q4(binary2bcd_1_q4), .q3(binary2bcd_1_q3),
    .q2(binary2bcd_1_q2), .q1(binary2bcd_1_q1), .q0(binary2bcd_1_q0));  // open: b5, b4, b3, b2, b1, b0
  _7_Segment_Display u_7_segment_display_1 (.g(n7448_2_p1));  // open: f, a, b, e, d, c, dp
  // _7448 7448_1: pin names not known; wires that end beside it: binary2bcd_1_q9, binary2bcd_1_q8, binary2bcd_1_q1, binary2bcd_1_q2, 1'b1, 1'b1, binary2bcd_1_q3, binary2bcd_1_q0, 1'b0, 1'b1, n7448_1_p11, n7448_1_p12, n7448_1_p13, n7448_1_p14, n7448_1_p15, n7448_1_p16, n7448_1_p17
  // _7448 7448_2: pin names not known; wires that end beside it: n7448_2_p1, binary2bcd_1_q5, binary2bcd_1_q6, 1'b1, binary2bcd_1_q7, binary2bcd_1_q4, 1'b0, 1'b1, n7448_2_p9, n7448_2_p10, n7448_2_p11, n7448_2_p12, n7448_2_p13, n7448_2_p14, n7448_2_p15
  _7_Segment_Display u_7_segment_display_2 (
    .g(n7448_2_p10), .f(n7448_2_p9), .a(n7448_2_p11), .b(n7448_2_p12), .e(n7448_2_p15), .d(n7448_2_p14),
    .c(n7448_2_p13));  // open: dp
  _7_Segment_Display u_7_segment_display_3 (
    .g(n7448_1_p12), .f(n7448_1_p11), .a(n7448_1_p13), .b(n7448_1_p14), .e(n7448_1_p17), .d(n7448_1_p16),
    .c(n7448_1_p15));  // open: dp
endmodule
