// Logisim project PROJECT.circ as structural Verilog
module _1_bit_comp (
  input  in_1,
  input  in_2,
  output A1,
  output A_B
);

  wire b_t, c;

  // _7408 7408_1: pin names not known; wires that end beside it: b_t, in_1, A1, 1'b0, 1'b1
  // _7404 7404_1: pin names not known; wires that end beside it: in_2, b_t, c, A_B, 1'b0, 1'b1
  // _7486 7486_1: pin names not known; wires that end beside it: in_1, in_2, c, 1'b0, 1'b1

  // Other names for the same wires on the sheet: a = in_1; b = in_2
endmodule

module _3_bit_comp (
  input  A0,
  input  A1,
  input  B0,
  input  B1,
  output A_EQ_B,
  output A_BIG,
  output B_A
);

  wire A_0, A_0_t, A_1, A_1_t, C2, n7404_1_p3;

  _1_bit_comp u_1_bit_comp_1 (.in_1(A0), .in_2(B0), .A1(A_0_t), .A_B(A_0));
  // _7408 7408_1: pin names not known; wires that end beside it: A_1, A_0, A_EQ_B, 1'b0, 1'b1, A_1, A_0_t, C2
  _1_bit_comp u_1_bit_comp_2 (.in_1(A1), .in_2(B1), .A1(A_1_t), .A_B(A_1));
  // _7404 7404_1: pin names not known; wires that end beside it: 1'b0, 1'b1, n7404_1_p3, B_A
  // _7432 7432_1: pin names not known; wires that end beside it: A_1_t, C2, A_BIG
  // _7486 7486_1: pin names not known; wires that end beside it: A_EQ_B, A_BIG, n7404_1_p3, 1'b0, 1'b1

  // Other names for the same wires on the sheet: A_B = B_A; A_B_t = A_EQ_B; A_B_t_t = A_BIG
endmodule

// C
module CONTROLS (
  input  as,
  input  ADD_0__SUB1,
  input  bs,
  output control
);

  wire c1, c1_t;

  // _7486 7486_1: pin names not known; wires that end beside it: as, bs, c1, 1'b0, 1'b1
  // _7404 7404_1: pin names not known; wires that end beside it: c1, c1_t, 1'b0, 1'b1
  _2x1_MUX u_2x1_mux_1 (.i0(c1), .i1(c1_t), .o(control), .s0(ADD_0__SUB1));
endmodule

// 4X1
module _4X1_MUX (
  input  s0,
  input  i0,
  input  i2,
  input  i1,
  input  i3,
  input  s1,
  output o
);

  wire n2x1_mux_1_o, n2x1_mux_2_o;

  _2x1_MUX u_2x1_mux_1 (.i0(i2), .i1(i3), .o(n2x1_mux_1_o), .s0(s0));
  _2x1_MUX u_2x1_mux_2 (.i0(i0), .i1(i1), .o(n2x1_mux_2_o), .s0(s0));
  _2x1_MUX u_2x1_mux_3 (.i0(n2x1_mux_2_o), .i1(n2x1_mux_1_o), .o(o), .s0(s1));
endmodule

// 2x1
module _2x1_MUX (
  input  i0,
  input  s0,
  input  i1,
  output o
);

  wire n7404_1_p2, n7408_1_p3, n7408_1_p6;

  // _7404 7404_1: pin names not known; wires that end beside it: s0, n7404_1_p2
  // _7408 7408_1: pin names not known; wires that end beside it: i0, n7404_1_p2, n7408_1_p3, s0, i1, n7408_1_p6
  // _7432 7432_1: pin names not known; wires that end beside it: n7408_1_p6, n7408_1_p3, o
endmodule

module SIGN (
  input  A1,
  input  A0,
  input  ADD_0__SUB1,
  input  A2,
  input  B2,
  input  B1,
  input  B0,
  input  AS,
  input  BS,
  output SIGN
);

  wire A_B, A_B_t, A_B_t_t, B_A, C, minus_ve_flag, n7408_1_p3, O1, plus_ve_flag, S1;

  // _3_bit_comp 3_bit_comp_1: pin names not known; wires that end beside it: A1, A0, A2, B2, B1, B0, A_B_t, A_B_t_t, B_A
  _4X1_MUX MUX (.i0(A_B), .i2(1'b0), .i1(1'b1), .i3(A_B_t_t), .o(minus_ve_flag), .s0(AS), .s1(BS));
  _4X1_MUX u_4x1_mux_1 (.i0(1'b0), .i2(S1), .i1(1'b0), .i3(1'b0), .o(O1), .s0(A_B_t), .s1(C));
  _4X1_MUX MUX_2 (.i0(1'b0), .i2(A_B), .i1(A_B_t_t), .i3(1'b1), .o(plus_ve_flag), .s0(AS), .s1(BS));
  _2x1_MUX u_2x1_mux_1 (.i0(plus_ve_flag), .i1(minus_ve_flag), .o(S1), .s0(ADD_0__SUB1));
  _2x1_MUX u_2x1_mux_2 (.i0(1'b1), .i1(O1), .o(SIGN), .s0(n7408_1_p3));
  // _7404 7404_1: pin names not known; wires that end beside it: A_B_t_t, A_B, 1'b0, 1'b1
  CONTROLS controls_1 (.as(AS), .bs(BS), .ADD_0__SUB1(ADD_0__SUB1), .control(C));
  // _7408 7408_1: pin names not known; wires that end beside it: AS, BS, n7408_1_p3

  // Other names for the same wires on the sheet: ADD = ADD_0__SUB1
endmodule

module full_adder (
  input  B,
  input  A,
  input  c,
  output sum,
  output Carry
);

  wire n7432_1_p1, n7432_1_p2, n7486_1_p3;

  // _7486 7486_1: pin names not known; wires that end beside it: A, B, n7486_1_p3, n7486_1_p3, c, sum, 1'b0, 1'b1
  // _7432 7432_1: pin names not known; wires that end beside it: n7432_1_p1, n7432_1_p2, Carry, 1'b0, 1'b1
  // _7408 7408_1: pin names not known; wires that end beside it: c, n7486_1_p3, n7432_1_p1, B, A, n7432_1_p2, 1'b0, 1'b1
endmodule

module add_subtract (
  input  b0,
  input  b2,
  input  b1,
  input  a2,
  input  a0,
  input  a1,
  input  control,
  output carr,
  output s1,
  output s2,
  output s3
);

  wire full_adder_2_carry, full_adder_3_carry, n7486_1_p3, n7486_1_p6, n7486_1_p11;

  full_adder full_adder_1 (.B(n7486_1_p11), .A(a2), .c(full_adder_2_carry), .sum(s3), .Carry(carr));
  full_adder full_adder_2 (.B(n7486_1_p6), .A(a1), .c(full_adder_3_carry), .sum(s2), .Carry(full_adder_2_carry));
  full_adder full_adder_3 (.B(n7486_1_p3), .A(a0), .c(control), .sum(s1), .Carry(full_adder_3_carry));
  // _7486 7486_1: pin names not known; wires that end beside it: control, b0, n7486_1_p3, control, b1, n7486_1_p6, 1'b0, 1'b1, control, b2, n7486_1_p11
endmodule

// C3
module DEBUG (
  input  B2,
  input  B1,
  input  B0,
  input  A2,
  input  A1,
  input  A0,
  input  A0_S1,
  input  AS,
  input  BS,
  output O4,
  output O3,
  output O2,
  output O1,
  output CONTROL
);

  wire A_B, A_BIG, B_BIG, C1, C2, C3;

  CONTROLS controls_1 (.as(AS), .bs(BS), .ADD_0__SUB1(A0_S1), .control(CONTROL));
  add_subtract add_subtract_1 (
    .b0(B0), .b2(B2), .a0(A0), .a1(A1), .s1(C1), .s3(C3), .a2(A2), .s2(C2), .control(CONTROL), .b1(B1),
    .carr(O4));
  // _7486 7486_1: pin names not known; wires that end beside it: C3, B_BIG, O3, 1'b0, 1'b1, C1, B_BIG, O1, C2, B_BIG, O2
  // _3_bit_comp 3_bit_comp_1: pin names not known; wires that end beside it: A1, A0, A2, B2, B1, B0, A_B, A_BIG, B_BIG

  // Other names for the same wires on the sheet: C = CONTROL; S1 = O1; S2 = O2; S3 = O3; C4 = O4; S4 = O4
endmodule

module ADD_1 (
  input  B1,
  input  B2,
  input  B3,
  input  B4,
  output O1,
  output O2,
  output O3,
  output O4
);

  wire F2, n7408_1_p11, n7408_2_p11, n7432_2_p5, P1, P2, P3, P4, P5, P6, S1S2, S2_t, S2S1, S3_nS2S1, S3_t,
       S3S1, S3S2, S4_t, S4S2;

  // _7404 7404_1: pin names not known; wires that end beside it: B1, O1, B2, S2_t, B3, S3_t, 1'b0, 1'b1, B4, S4_t
  // _7408 7408_1: pin names not known; wires that end beside it: S2_t, B1, S1S2, O1, B2, S2S1, 1'b0, 1'b1, S3_t, B2, n7408_1_p11, n7408_1_p11, B1, S3_nS2S1
  // _7408 7408_2: pin names not known; wires that end beside it: B3, S2_t, S3S2, B3, O1, S3S1, 1'b0, 1'b1, S4_t, B3, n7408_2_p11, n7408_2_p11, B1, F2
  // _7408 7408_3: pin names not known; wires that end beside it: B2, F2, P2, 1'b0, 1'b1
  // _7432 7432_1: pin names not known; wires that end beside it: S2S1, S1S2, O2, S3_nS2S1, S3S2, P1, 1'b0, 1'b1, P1, S3S1, O3, P3, S4S2, P4
  // _7432 7432_2: pin names not known; wires that end beside it: 1'b0, 1'b1, P4, P5, n7432_2_p5, n7432_2_p5, P6, O4
  // _7408 7408_4: pin names not known; wires that end beside it: P2, B1, P3, B4, S2_t, S4S2, 1'b0, 1'b1, B4, S3_t, P5, B4, O1, P6

  // Other names for the same wires on the sheet: S1 = B1; S1_t = O1; S2 = B2; S3 = B3; S4 = B4
endmodule
