// Logisim project RemainderProject.circ as structural Verilog
module half_adder (
  input  in_1,
  input  in_2,
  output cout,
  output s1
);

  // _7486 7486_1: pin names not known; wires that end beside it: in_1, in_2, s1
  // _7408 7408_1: pin names not known; wires that end beside it: in_1, in_2, cout

  // Other names for the same wires on the sheet: x = in_1; y = in_2
endmodule

module full_adder_2 (
  input  in_1,
  input  in_2,
  input  in_3,
  output out_4,
  output out_5
);

  wire half_adder_1_cout, half_adder_1_s1, half_adder_2_cout;

  half_adder half_adder_1 (.in_1(in_1), .in_2(in_2), .cout(half_adder_1_cout), .s1(half_adder_1_s1));
  half_adder half_adder_2 (.in_1(half_adder_1_s1), .in_2(in_3), .cout(half_adder_2_cout), .s1(out_4));
  // _7432 7432_1: pin names not known; wires that end beside it: half_adder_2_cout, half_adder_1_cout, out_5
endmodule

module _2x1 (
  input  i0,
  input  i1,
  input  s0,
  output out_4
);

  wire n7404_1_p2, n7408_1_p3, n7408_1_p6;

  // _7404 7404_1: pin names not known; wires that end beside it: s0, n7404_1_p2
  // _7408 7408_1: pin names not known; wires that end beside it: i0, n7404_1_p2, n7408_1_p3, s0, i1, n7408_1_p6
  // _7432 7432_1: pin names not known; wires that end beside it: n7408_1_p6, n7408_1_p3, out_4
endmodule

module Remainder (
  input  As,
  input  A2,
  input  A1,
  input  A0,
  input  Bs,
  input  B2,
  input  B1,
  input  B0,
  output Cs,
  output C2,
  output C1,
  output C0
);

  wire A1_out_4, A2_2_out_4, A2_out_4, subtractor_1_ans, subtractor_1_bout, subtractor_2_ans,
       subtractor_2_bout, subtractor_3_ans, subtractor_3_bout, subtractor_4_ans, subtractor_4_bout,
       subtractor_5_ans, subtractor_5_bout, subtractor_6_ans, subtractor_6_bout, subtractor_7_ans,
       subtractor_7_bout, subtractor_8_ans, subtractor_8_bout, subtractor_9_ans, subtractor_9_bout,
       zero_out_4;

  Subtractor subtractor_1 (.A(A2), .B(B0), .Bin(1'b0), .Bout(subtractor_1_bout), .Ans(subtractor_1_ans));
  Subtractor subtractor_2 (.A(1'b0), .B(B1), .Bin(subtractor_1_bout), .Bout(subtractor_2_bout), .Ans(subtractor_2_ans));
  Subtractor subtractor_3 (.A(1'b0), .B(B2), .Bin(subtractor_2_bout), .Bout(subtractor_3_bout), .Ans(subtractor_3_ans));
  _2x1 u_A2 (.i0(subtractor_1_ans), .i1(A2), .s0(subtractor_3_bout), .out_4(A2_out_4));
  _2x1 zero (.i0(subtractor_2_ans), .i1(1'b0), .s0(subtractor_3_bout), .out_4(zero_out_4));
  Subtractor subtractor_4 (.A(A1), .B(B0), .Bin(1'b0), .Bout(subtractor_4_bout), .Ans(subtractor_4_ans));
  Subtractor subtractor_5 (
    .A(A2_out_4), .B(B1), .Bin(subtractor_4_bout), .Bout(subtractor_5_bout), .Ans(subtractor_5_ans));
  Subtractor subtractor_6 (
    .A(zero_out_4), .B(B2), .Bin(subtractor_5_bout), .Bout(subtractor_6_bout), .Ans(subtractor_6_ans));
  _2x1 u_A1 (.i0(subtractor_4_ans), .i1(A1), .s0(subtractor_6_bout), .out_4(A1_out_4));
  _2x1 A2_2 (.i0(subtractor_5_ans), .i1(A2_out_4), .s0(subtractor_6_bout), .out_4(A2_2_out_4));
  Subtractor subtractor_7 (.A(A0), .B(B0), .Bin(1'b0), .Bout(subtractor_7_bout), .Ans(subtractor_7_ans));
  Subtractor subtractor_8 (
    .A(A1_out_4), .B(B1), .Bin(subtractor_7_bout), .Bout(subtractor_8_bout), .Ans(subtractor_8_ans));
  Subtractor subtractor_9 (
    .A(A2_2_out_4), .B(B2), .Bin(subtractor_8_bout), .Bout(subtractor_9_bout), .Ans(subtractor_9_ans));
  _2x1 u_C0 (.i0(subtractor_7_ans), .i1(A0), .s0(subtractor_9_bout), .out_4(C0));
  _2x1 u_2x1_1 (.i0(subtractor_8_ans), .i1(A1_out_4), .s0(subtractor_9_bout), .out_4(C1));
  _2x1 u_2x1_2 (.i0(subtractor_9_ans), .i1(A2_2_out_4), .s0(subtractor_9_bout), .out_4(C2));

  assign Cs = As;
endmodule

// Flags
module Div0 (
  input  B2,
  input  B1,
  input  B0,
  output Div0
);

  wire OR_p3, OR_p6;

  // _7432 OR: pin names not known; wires that end beside it: B2, B1, OR_p3, OR_p3, B0, OR_p6, 1'b0, 1'b1
  // _7404 7404_1: pin names not known; wires that end beside it: OR_p6, Div0, 1'b0, 1'b1
endmodule

// Remainder
module Final_step (
  input  As,
  input  A2,
  input  A1,
  input  A0,
  input  Bs,
  input  B2,
  input  B1,
  input  B0,
  output Div0,
  output Cs,
  output C2,
  output C1,
  output C0
);

  wire C0_t, C1_t, C2_t;

  Remainder remainder_1 (
    .As(As), .A2(A2), .A1(A1), .A0(A0), .Bs(Bs), .B2(B2), .B1(B1), .B0(B0), .Cs(Cs), .C2(C2_t), .C1(C1_t),
    .C0(C0_t));
  Div0 div0_1 (.B2(B2), .B1(B1), .B0(B0), .Div0(Div0));
  // _74157 74157_1: pin names not known; wires that end beside it: Div0, C0_t, 1'b0, C0, C1_t, 1'b0, C1, 1'b0, 1'b1, 1'b0, C2_t, 1'b0, C2, 1'b0, 1'b0
endmodule

module Final_Rem (
  input  As,
  input  A2,
  input  A1,
  input  A0,
  input  Bs,
  input  B2,
  input  B1,
  input  B0,
  output Div0,
  output Cs,
  output C2,
  output C1,
  output C0
);

  Final_step Final (
    .As(As), .A2(A2), .A1(A1), .A0(A0), .Bs(Bs), .B2(B2), .B1(B1), .B0(B0), .Div0(Div0), .Cs(Cs), .C2(C2),
    .C1(C1), .C0(C0));
endmodule

// X-B
module Subtractor (
  input  Bin,
  input  A,
  input  B,
  output Ans,
  output Bout
);

  wire AND_p3, AND_p6, NOT_p2, NOT_p4, XOR_p3;

  // _7486 XOR: pin names not known; wires that end beside it: A, B, XOR_p3, XOR_p3, Bin, Ans, 1'b0, 1'b1
  // _7404 NOT: pin names not known; wires that end beside it: A, NOT_p2, XOR_p3, NOT_p4, 1'b0, 1'b1
  // _7408 AND: pin names not known; wires that end beside it: NOT_p2, B, AND_p3, NOT_p4, Bin, AND_p6, 1'b0, 1'b1
  // _7432 OR: pin names not known; wires that end beside it: AND_p3, AND_p6, Bout, 1'b0, 1'b1
endmodule
