// Logisim project test 4x1.circ as structural Verilog
module half_adder (
  input  in_1,
  input  in_2,
  output cout,
  output s1
);

  // _7486 7486_1: pin names not known; wires that end beside it: in_1, in_2, s1
  // _7408 7408_1: pin names not known; wires that end beside it: in_1, in_2, cout

  // Other names for the same wires on the sheet: x = in_1; y = in_2
endmodule

module full_adder_2 (
  input  in_1,
  input  in_2,
  input  in_3,
  output out_4,
  output out_5
);

  wire half_adder_1_cout, half_adder_1_s1, half_adder_2_cout;

  half_adder half_adder_1 (.in_1(in_1), .in_2(in_2), .cout(half_adder_1_cout), .s1(half_adder_1_s1));
  half_adder half_adder_2 (.in_1(half_adder_1_s1), .in_2(in_3), .cout(half_adder_2_cout), .s1(out_4));
  // _7432 7432_1: pin names not known; wires that end beside it: half_adder_2_cout, half_adder_1_cout, out_5
endmodule

module _2x1 (
  input  i0,
  input  s0,
  input  i1,
  output o
);

  wire n7404_1_p2, n7408_1_p3, n7408_1_p6;

  // _7404 7404_1: pin names not known; wires that end beside it: s0, n7404_1_p2
  // _7408 7408_1: pin names not known; wires that end beside it: i0, n7404_1_p2, n7408_1_p3, s0, i1, n7408_1_p6
  // _7432 7432_1: pin names not known; wires that end beside it: n7408_1_p6, n7408_1_p3, o
endmodule

module _4x1 (
  input  i0,
  input  i1,
  input  i2,
  input  i3,
  input  s1,
  input  s0,
  output o
);

  wire n2x1_1_o, n2x1_2_o;

  _2x1 u_2x1_1 (.i0(i2), .i1(i3), .o(n2x1_1_o), .s0(s0));
  _2x1 u_2x1_2 (.i0(i0), .i1(i1), .o(n2x1_2_o), .s0(s0));
  _2x1 u_2x1_3 (.i0(n2x1_2_o), .i1(n2x1_1_o), .o(o), .s0(s1));
endmodule

module f (
  input  a,
  input  c,
  input  b,
  output f
);

  wire n4x1_1_p4;

  // _4x1 4x1_1: pin names not known; wires that end beside it: 1'b0, 1'b1, c, n4x1_1_p4, f, a, b
  // _7404 7404_1: pin names not known; wires that end beside it: c, n4x1_1_p4
endmodule

module _8x1_MUX (
  input  i0,
  input  i1,
  input  i2,
  input  s2,
  input  i3,
  input  s1,
  input  i4,
  input  s0,
  input  i5,
  input  i6,
  input  i7,
  output o
);

  wire n4x1_1_p5, n4x1_2_p5;

  // _4x1 4x1_1: pin names not known; wires that end beside it: i0, i1, i2, i3, n4x1_1_p5, s0, s1
  // _4x1 4x1_2: pin names not known; wires that end beside it: i4, i5, i6, i7, n4x1_2_p5, s0, s1
  _2x1 u_2x1_1 (.i0(n4x1_1_p5), .i1(n4x1_2_p5), .o(o), .s0(s2));
endmodule

// C2-R
module Remainder_C2 (
  input  A2,
  input  A1,
  input  B2,
  input  A0,
  input  B1,
  input  B0,
  output C2
);

  wire AND_p4, AND_p7, AND_p10, AND_p12;

  // _7408 AND: pin names not known; wires that end beside it: B0, B2, B1, AND_p4, AND_p4, B0, AND_p7, 1'b0, 1'b1, AND_p10, B2, AND_p12
  _8x1_MUX u_8x1_mux_1 (
    .i0(1'b0), .i1(1'b0), .i2(1'b0), .i3(1'b0), .i4(AND_p12), .i5(AND_p7), .i6(AND_p4), .i7(1'b0), .o(C2),
    .s2(A2), .s1(A1), .s0(A0));
  // _7432 OR: pin names not known; wires that end beside it: B0, B1, AND_p10, 1'b0, 1'b1
endmodule

// C1-R
module Remainder_C1 (
  input  A2,
  input  A1,
  input  A0,
  input  B2,
  input  B1,
  input  B0,
  output C1
);

  wire AND_2_p3, AND_2_p8, AND_p3, AND_p6, AND_p8, AND_p11, NOT_p4, NOT_p7, NOT_p8, OR_p3;

  // _7408 AND: pin names not known; wires that end beside it: B1, B0, AND_p3, 1'b0, 1'b1, AND_p6, B1, AND_p8, AND_p8, B0, AND_p11
  _8x1_MUX u_8x1_mux_1 (
    .i0(1'b0), .i1(OR_p3), .i2(1'b0), .i3(B2), .i4(1'b0), .i5(AND_2_p3), .i6(AND_p11), .i7(AND_2_p8), .o(C1),
    .s2(A2), .s1(A1), .s0(A0));
  // _7432 OR: pin names not known; wires that end beside it: AND_p3, B2, OR_p3, 1'b0, 1'b1
  // _7404 NOT: pin names not known; wires that end beside it: B2, AND_p6, B1, NOT_p4, 1'b0, 1'b1, NOT_p7, NOT_p8
  // _7486 7486_1: pin names not known; wires that end beside it: B1, B0, NOT_p7, 1'b0, 1'b1
  // _7408 AND_2: pin names not known; wires that end beside it: NOT_p8, B2, AND_2_p3, 1'b0, 1'b1, NOT_p4, B2, AND_2_p8
endmodule

// C0-R
module Remainder_C0 (
  input  A2,
  input  B2,
  input  A1,
  input  B1,
  input  A0,
  input  B0,
  output C0
);

  wire AND_2_p11, AND_2_p14, AND_3_p8, AND_3_p11, AND_p1, AND_p4, AND_p6, AND_p7, AND_p9, NOT_p2, NOT_p8,
       OR_2_p3, OR_2_p6, OR_2_p9, OR_2_p11, OR_2_p12, OR_2_p13, OR_2_p14, OR_p4;

  // _7408 AND: pin names not known; wires that end beside it: AND_p1, 1'b0, 1'b1, AND_p4, B2, AND_p6, AND_p7, B1, AND_p9
  // _7432 OR: pin names not known; wires that end beside it: AND_p1, AND_p6, AND_p9, OR_p4, 1'b0, 1'b1
  // _7404 NOT: pin names not known; wires that end beside it: B2, NOT_p2, B0, AND_p4, 1'b0, 1'b1, B1, NOT_p8, B2, AND_p7
  // _7432 OR_2: pin names not known; wires that end beside it: B2, B1, OR_2_p3, B2, B1, OR_2_p6, 1'b0, 1'b1, OR_2_p9, B2, OR_2_p11, OR_2_p12, OR_2_p13, OR_2_p14
  // _7408 AND_2: pin names not known; wires that end beside it: AND_p4, B1, OR_2_p9, AND_p4, OR_2_p6, OR_2_p13, 1'b0, 1'b1, NOT_p2, B1, AND_2_p11, AND_2_p11, B0, AND_2_p14
  // _7408 AND_3: pin names not known; wires that end beside it: B2, B1, OR_2_p12, 1'b0, 1'b1, NOT_p8, B2, AND_3_p8, AND_3_p8, B0, AND_3_p11
  _8x1_MUX u_8x1_mux_1 (
    .i0(1'b0), .i1(1'b0), .i2(OR_2_p3), .i3(OR_2_p11), .i4(AND_2_p14), .i5(AND_3_p11), .i6(OR_2_p14),
    .i7(OR_p4), .o(C0), .s2(A2), .s1(A1), .s0(A0));
endmodule

module Remainder (
  input  Bs,
  input  As,
  input  B2,
  input  A2,
  input  B1,
  input  A1,
  input  B0,
  input  A0,
  output Cs,
  output C2,
  output C1,
  output C0
);

  Remainder_C2 remainder_c2_1 (.B2(B2), .B1(B1), .B0(B0), .C2(C2), .A2(A2), .A1(A1), .A0(A0));
  Remainder_C1 remainder_c1_1 (.B2(B2), .B1(B1), .B0(B0), .C1(C1), .A2(A2), .A1(A1), .A0(A0));
  Remainder_C0 remainder_c0_1 (.B2(B2), .B1(B1), .B0(B0), .C0(C0), .A2(A2), .A1(A1), .A0(A0));

  assign Cs = As;
endmodule

module Fzero (
  input  C2,
  input  C1,
  input  C0,
  output Fzero
);

  wire n7432_1_p3, n7432_1_p6;

  // _7404 7404_1: pin names not known; wires that end beside it: 1'b1
  // _7432 7432_1: pin names not known; wires that end beside it: C2, C1, n7432_1_p3, n7432_1_p3, C0, n7432_1_p6, 1'b0, 1'b1, n7432_1_p6, Fzero, 1'b0
endmodule

module Fdiv0 (
  input  B2,
  input  B1,
  input  B0,
  output Fdiv0
);

  wire n7432_1_p3, n7432_1_p6;

  // _7432 7432_1: pin names not known; wires that end beside it: B2, B1, n7432_1_p3, n7432_1_p3, B0, n7432_1_p6, 1'b0, 1'b1
  // _7404 7404_1: pin names not known; wires that end beside it: n7432_1_p6, Fdiv0, 1'b0, 1'b1
endmodule
